// Logisim project Nguyen_Nam_Tung_103181157_Assign1.circ as structural Verilog: 9 circuits, main circuit main_clock
module main_clock (
  input  set_time,
  input  turn_on_alarm,
  input  set_alarm,
  input  power,
  input  set_AMPM_for_alarm
);

  wire compare_1_main_alarm, compare_1_main_ampm, hour_increment_out, minute_increment_out, not_1_out;
  wire [3:0] compare_1_main_hour_0a, compare_1_main_hour_a0, compare_1_main_min_0a, compare_1_main_min_a0;

  Button minute_increment (.out(minute_increment_out));
  Button hour_increment (.out(hour_increment_out));
  compare compare_1 (
    .set_alarm(set_alarm), .hour_plus(hour_increment_out), .power(power), .set_time(set_time),
    .minute_plus(minute_increment_out), .set_ampm(set_AMPM_for_alarm), .alarm_on(turn_on_alarm),
    .main_min_a0(compare_1_main_min_a0), .main_min_0a(compare_1_main_min_0a),
    .main_hour_a0(compare_1_main_hour_a0), .main_hour_0a(compare_1_main_hour_0a),
    .main_alarm(compare_1_main_alarm), .main_ampm(compare_1_main_ampm));
  Hex_Digit_Display hex_digit_display_1 (.value(compare_1_main_hour_a0));  // open: dp
  Hex_Digit_Display hex_digit_display_2 (.value(compare_1_main_hour_0a));  // open: dp
  Hex_Digit_Display hex_digit_display_3 (.value(compare_1_main_min_a0));  // open: dp
  Hex_Digit_Display hex_digit_display_4 (.value(compare_1_main_min_0a));  // open: dp
  LED alarm (.in(compare_1_main_alarm));
  LED PM (.in(compare_1_main_ampm));
  not not_1 (not_1_out, compare_1_main_ampm);
  LED AM (.in(not_1_out));

  // Notes on the sheet:
  //   m+
  //   h+
endmodule

module minute (
  input  power,
  input  set_time,
  input  minute_plus,
  input  in_4,
  output reach59,
  output minute_a1,
  output minute_a2,
  output minute_a4,
  output minute_a8,
  output minute_1a,
  output minute_2a,
  output minute_4a
);

  wire and_1_out, and_2_out, and_3_out, and_4_out, and_5_out, and_6_out, and_8_out, and_9_out, and_10_out,
       and_11_out, j_k_ff_1_q, j_k_ff_2_q, j_k_ff_3_q, j_k_ff_4_q, j_k_ff_5_q, j_k_ff_6_q, j_k_ff_7_q,
       not_1_out, or_1_out, or_2_out, s_clock_out;

  Clock s_clock (.out(s_clock_out));
  and and_1 (and_1_out, power, not_1_out);
  not not_1 (not_1_out, set_time);
  and and_2 (and_2_out, not_1_out, s_clock_out);
  or or_1 (or_1_out, and_1_out, minute_plus);
  or or_2 (or_2_out, and_2_out, minute_plus);
  J_K_Flip_Flop j_k_ff_1 (
    .J(or_1_out), .K(or_1_out), .clk(or_2_out), .Q(j_k_ff_1_q), .reset(and_6_out));  // open: Qn, preset
  D_Flip_Flop d_ff_1 (.D(j_k_ff_1_q), .clk(or_2_out), .Q(minute_a1));  // open: Qn, preset, reset
  J_K_Flip_Flop j_k_ff_2 (
    .J(j_k_ff_1_q), .K(j_k_ff_1_q), .clk(or_2_out), .Q(j_k_ff_2_q), .reset(and_6_out));  // open: Qn, preset
  D_Flip_Flop d_ff_2 (.D(j_k_ff_2_q), .clk(or_2_out), .Q(minute_a2));  // open: Qn, preset, reset
  and and_3 (and_3_out, j_k_ff_1_q, j_k_ff_2_q);
  J_K_Flip_Flop j_k_ff_3 (
    .J(and_3_out), .K(and_3_out), .clk(or_2_out), .Q(j_k_ff_3_q), .reset(and_6_out));  // open: Qn, preset
  D_Flip_Flop d_ff_3 (.D(j_k_ff_3_q), .clk(or_2_out), .Q(minute_a4));  // open: Qn, preset, reset
  J_K_Flip_Flop j_k_ff_4 (
    .J(and_4_out), .K(and_4_out), .clk(or_2_out), .Q(j_k_ff_4_q), .reset(and_6_out));  // open: Qn, preset
  and and_4 (and_4_out, and_3_out, j_k_ff_3_q);
  D_Flip_Flop d_ff_4 (.D(j_k_ff_4_q), .clk(or_2_out), .Q(minute_a8));  // open: Qn, preset, reset
  and and_5 (and_5_out, j_k_ff_1_q, j_k_ff_4_q);
  and and_6 (and_6_out, j_k_ff_2_q, j_k_ff_4_q);
  Hex_Digit_Display hex_digit_display_1 (.value({in_4, minute_4a, minute_2a, minute_1a}));  // open: dp
  J_K_Flip_Flop j_k_ff_5 (
    .J(and_5_out), .K(and_5_out), .clk(or_2_out), .Q(j_k_ff_5_q), .reset(and_11_out));  // open: Qn, preset
  Hex_Digit_Display hex_digit_display_2 (.value({minute_a8, minute_a4, minute_a2, minute_a1}));  // open: dp
  and and_7 (reach59, and_5_out, and_8_out);
  and and_8 (and_8_out, j_k_ff_5_q, j_k_ff_7_q);
  D_Flip_Flop d_ff_5 (.D(j_k_ff_5_q), .clk(or_2_out), .Q(minute_1a));  // open: Qn, preset, reset
  and and_9 (and_9_out, and_5_out, j_k_ff_5_q);
  J_K_Flip_Flop j_k_ff_6 (
    .J(and_9_out), .K(and_9_out), .clk(or_2_out), .Q(j_k_ff_6_q), .reset(and_11_out));  // open: Qn, preset
  D_Flip_Flop d_ff_6 (.D(j_k_ff_6_q), .clk(or_2_out), .Q(minute_2a));  // open: Qn, preset, reset
  and and_10 (and_10_out, and_9_out, j_k_ff_6_q);
  J_K_Flip_Flop j_k_ff_7 (
    .J(and_10_out), .K(and_10_out), .clk(or_2_out), .Q(j_k_ff_7_q), .reset(and_11_out));  // open: Qn, preset
  D_Flip_Flop d_ff_7 (.D(j_k_ff_7_q), .clk(or_2_out), .Q(minute_4a));  // open: Qn, preset, reset
  and and_11 (and_11_out, j_k_ff_6_q, j_k_ff_7_q);

  // Notes on the sheet:
  //   Reach 9
  //   Reset at 10
  //   Reach 5
  //   Reset at 6
endmodule

module hour (
  input  input_at_59,
  input  hour_plus,
  input  set_time,
  input  in_4,
  output hour_1a,
  output ampm,
  output hour_a1,
  output hour_a2,
  output hour_a4,
  output hour_a8
);

  wire and_1_out, and_2_out, and_3_out, and_4_out, and_5_out, and_6_out, and_7_out, and_8_out, clock_1_out,
       j_k_ff_1_q, j_k_ff_2_q, j_k_ff_3_q, j_k_ff_4_q, j_k_ff_5_q, j_k_ff_6_q, not_1_out, or_1_out, or_2_out,
       or_3_out;

  Clock clock_1 (.out(clock_1_out));
  not not_1 (not_1_out, set_time);
  or or_1 (or_1_out, input_at_59, set_time);
  and and_1 (and_1_out, not_1_out, clock_1_out);
  or or_2 (or_2_out, hour_plus, and_1_out);
  J_K_Flip_Flop j_k_ff_1 (.J(or_1_out), .K(or_1_out), .clk(or_2_out), .Q(j_k_ff_1_q));  // open: Qn, preset, reset
  J_K_Flip_Flop j_k_ff_2 (
    .J(and_2_out), .K(and_2_out), .clk(or_2_out), .Q(j_k_ff_2_q), .reset(and_5_out));  // open: Qn, preset
  and and_2 (and_2_out, j_k_ff_5_q, and_3_out);
  D_Flip_Flop d_ff_1 (.D(j_k_ff_1_q), .clk(or_2_out), .Q(hour_a1));  // open: Qn, preset, reset
  D_Flip_Flop d_ff_2 (.D(j_k_ff_2_q), .clk(or_2_out), .Q(hour_1a));  // open: Qn, preset, reset
  J_K_Flip_Flop j_k_ff_3 (
    .J(and_3_out), .K(and_3_out), .clk(or_2_out), .Q(j_k_ff_3_q), .reset(or_3_out));  // open: Qn, preset
  and and_3 (and_3_out, or_1_out, j_k_ff_1_q);
  D_Flip_Flop d_ff_3 (.D(j_k_ff_3_q), .clk(or_2_out), .Q(hour_a2));  // open: Qn, preset, reset
  and and_4 (and_4_out, and_3_out, j_k_ff_3_q);
  J_K_Flip_Flop j_k_ff_4 (
    .J(and_4_out), .K(and_4_out), .clk(or_2_out), .Q(j_k_ff_4_q), .reset(or_3_out));  // open: Qn, preset
  D_Flip_Flop d_ff_4 (.D(j_k_ff_4_q), .clk(or_2_out), .Q(hour_a4));  // open: Qn, preset, reset
  and and_5 (and_5_out, hour_1a, j_k_ff_1_q, and_4_out);
  and and_6 (and_6_out, and_4_out, j_k_ff_4_q);
  D_Flip_Flop d_ff_5 (.D(j_k_ff_5_q), .clk(or_2_out), .Q(hour_a8));  // open: Qn, preset, reset
  J_K_Flip_Flop j_k_ff_5 (
    .J(and_6_out), .K(and_6_out), .clk(or_2_out), .Q(j_k_ff_5_q), .reset(or_3_out));  // open: Qn, preset
  and and_7 (and_7_out, j_k_ff_3_q, j_k_ff_5_q);
  or or_3 (or_3_out, and_7_out, and_5_out);
  Hex_Digit_Display hex_digit_display_1 (.value({{3{in_4}}, hour_1a}));  // open: dp
  and and_8 (and_8_out, hour_1a, or_1_out, j_k_ff_1_q);
  Hex_Digit_Display hex_digit_display_2 (.value({hour_a8, hour_a4, hour_a2, hour_a1}));  // open: dp
  J_K_Flip_Flop j_k_ff_6 (.J(and_8_out), .K(and_8_out), .clk(or_2_out), .Q(j_k_ff_6_q));  // open: Qn, preset, reset
  D_Flip_Flop d_ff_6 (.D(j_k_ff_6_q), .clk(or_2_out), .Q(ampm));  // open: Qn, preset, reset
  LED led_1 (.in(ampm));

  // Notes on the sheet:
  //   Change at 9:59
  //   11h59m
endmodule

module alarm_clock (
  input  in_1,
  input  hour_plus,
  input  min_plus,
  input  in_4,
  input  set_ampm_alarm,
  output hour_a4,
  output hour_a8,
  output hour_a2,
  output hour_a1,
  output hour_1a,
  output alarm_clock_ampm,
  output minute_a1,
  output minute_a2,
  output minute_a4,
  output minute_a8,
  output Alarm_ampm,
  output minute_1a,
  output minute_2a,
  output minute_4a
);

  wire alarm_hour_1_ampm, not_1_out, t_ff_1_q;

  T_Flip_Flop t_ff_1 (.T(set_ampm_alarm), .clk(set_ampm_alarm), .Q(t_ff_1_q));  // open: Qn, reset, preset
  D_Flip_Flop d_ff_1 (.D(t_ff_1_q), .clk(set_ampm_alarm), .Q(Alarm_ampm));  // open: Qn, preset, reset
  not not_1 (not_1_out, Alarm_ampm);
  alarm_minute alarm_minute_1 (
    .minute_plus(min_plus), .minute_a1(minute_a1), .minute_a2(minute_a2), .minute_a4(minute_a4),
    .minute_a8(minute_a8), .minute_1a(minute_1a), .minute_2a(minute_2a), .minute_4a(minute_4a));  // open: in_2, reach59
  LED AM (.in(not_1_out));
  LED PM (.in(Alarm_ampm));
  alarm_hour alarm_hour_1 (
    .hour_plus(hour_plus), .hour_1a(hour_1a), .ampm(alarm_hour_1_ampm), .hour_a1(hour_a1), .hour_a2(hour_a2),
    .hour_a4(hour_a4), .hour_a8(hour_a8));  // open: input_at_59, in_3
  Hex_Digit_Display hex_digit_display_1 (.value({{3{in_1}}, hour_1a}));  // open: dp
  Hex_Digit_Display hex_digit_display_2 (.value({hour_a8, hour_a4, hour_a2, hour_a1}));  // open: dp
  Hex_Digit_Display hex_digit_display_3 (.value({in_4, minute_4a, minute_2a, minute_1a}));  // open: dp
  Hex_Digit_Display hex_digit_display_4 (.value({minute_a8, minute_a4, minute_a2, minute_a1}));  // open: dp
  not not_2 (alarm_clock_ampm, alarm_hour_1_ampm);
  LED led_1 (.in(alarm_hour_1_ampm));
  LED led_2 (.in(alarm_clock_ampm));

  // Notes on the sheet:
  //   :
  //   AM
  //   PM
endmodule

module alarm_minute (
  input  minute_plus,
  input  in_2,
  output reach59,
  output minute_a1,
  output minute_a2,
  output minute_a4,
  output minute_a8,
  output minute_1a,
  output minute_2a,
  output minute_4a
);

  wire and_1_out, and_2_out, and_3_out, and_4_out, and_6_out, and_7_out, and_8_out, and_9_out, j_k_ff_1_q,
       j_k_ff_2_q, j_k_ff_3_q, j_k_ff_4_q, j_k_ff_5_q, j_k_ff_6_q, j_k_ff_7_q, not_1_out;

  not not_1 (not_1_out, minute_plus);
  J_K_Flip_Flop #(.trigger("falling")) j_k_ff_1 (
    .J(minute_plus), .K(minute_plus), .clk(not_1_out), .Q(j_k_ff_1_q), .reset(and_4_out));  // open: Qn, preset
  D_Flip_Flop d_ff_1 (.D(j_k_ff_1_q), .clk(not_1_out), .Q(minute_a1));  // open: Qn, preset, reset
  J_K_Flip_Flop #(.trigger("falling")) j_k_ff_2 (
    .J(j_k_ff_1_q), .K(j_k_ff_1_q), .clk(not_1_out), .Q(j_k_ff_2_q), .reset(and_4_out));  // open: Qn, preset
  D_Flip_Flop d_ff_2 (.D(j_k_ff_2_q), .clk(not_1_out), .Q(minute_a2));  // open: Qn, preset, reset
  and and_1 (and_1_out, j_k_ff_1_q, j_k_ff_2_q);
  J_K_Flip_Flop #(.trigger("falling")) j_k_ff_3 (
    .J(and_1_out), .K(and_1_out), .clk(not_1_out), .Q(j_k_ff_3_q), .reset(and_4_out));  // open: Qn, preset
  D_Flip_Flop d_ff_3 (.D(j_k_ff_3_q), .clk(not_1_out), .Q(minute_a4));  // open: Qn, preset, reset
  J_K_Flip_Flop #(.trigger("falling")) j_k_ff_4 (
    .J(and_2_out), .K(and_2_out), .clk(not_1_out), .Q(j_k_ff_4_q), .reset(and_4_out));  // open: Qn, preset
  and and_2 (and_2_out, and_1_out, j_k_ff_3_q);
  D_Flip_Flop d_ff_4 (.D(j_k_ff_4_q), .clk(not_1_out), .Q(minute_a8));  // open: Qn, preset, reset
  and and_3 (and_3_out, j_k_ff_1_q, j_k_ff_4_q);
  and and_4 (and_4_out, j_k_ff_2_q, j_k_ff_4_q);
  Hex_Digit_Display hex_digit_display_1 (.value({in_2, minute_4a, minute_2a, minute_1a}));  // open: dp
  J_K_Flip_Flop #(.trigger("falling")) j_k_ff_5 (
    .J(and_3_out), .K(and_3_out), .clk(not_1_out), .Q(j_k_ff_5_q), .reset(and_9_out));  // open: Qn, preset
  Hex_Digit_Display hex_digit_display_2 (.value({minute_a8, minute_a4, minute_a2, minute_a1}));  // open: dp
  and and_5 (reach59, and_3_out, and_6_out);
  and and_6 (and_6_out, j_k_ff_5_q, j_k_ff_7_q);
  D_Flip_Flop d_ff_5 (.D(j_k_ff_5_q), .clk(not_1_out), .Q(minute_1a));  // open: Qn, preset, reset
  and and_7 (and_7_out, and_3_out, j_k_ff_5_q);
  J_K_Flip_Flop #(.trigger("falling")) j_k_ff_6 (
    .J(and_7_out), .K(and_7_out), .clk(not_1_out), .Q(j_k_ff_6_q), .reset(and_9_out));  // open: Qn, preset
  D_Flip_Flop d_ff_6 (.D(j_k_ff_6_q), .clk(not_1_out), .Q(minute_2a));  // open: Qn, preset, reset
  and and_8 (and_8_out, and_7_out, j_k_ff_6_q);
  J_K_Flip_Flop #(.trigger("falling")) j_k_ff_7 (
    .J(and_8_out), .K(and_8_out), .clk(not_1_out), .Q(j_k_ff_7_q), .reset(and_9_out));  // open: Qn, preset
  D_Flip_Flop d_ff_7 (.D(j_k_ff_7_q), .clk(not_1_out), .Q(minute_4a));  // open: Qn, preset, reset
  and and_9 (and_9_out, j_k_ff_6_q, j_k_ff_7_q);

  // Notes on the sheet:
  //   Reach 9
  //   Reset at 10
  //   Reach 5
  //   Reset at 6
endmodule

module alarm_hour (
  input  input_at_59,
  input  hour_plus,
  input  in_3,
  output hour_1a,
  output ampm,
  output hour_a1,
  output hour_a2,
  output hour_a4,
  output hour_a8
);

  wire and_1_out, and_2_out, and_3_out, and_4_out, and_5_out, and_6_out, and_7_out, j_k_ff_1_q, j_k_ff_2_q,
       j_k_ff_3_q, j_k_ff_4_q, j_k_ff_5_q, j_k_ff_6_q, or_1_out, or_2_out;

  or or_1 (or_1_out, input_at_59, hour_plus);
  J_K_Flip_Flop #(.trigger("falling")) j_k_ff_1 (
    .J(or_1_out), .K(or_1_out), .clk(hour_plus), .Q(j_k_ff_1_q));  // open: Qn, preset, reset
  J_K_Flip_Flop #(.trigger("falling")) j_k_ff_2 (
    .J(and_1_out), .K(and_1_out), .clk(hour_plus), .Q(j_k_ff_2_q), .reset(and_4_out));  // open: Qn, preset
  and and_1 (and_1_out, j_k_ff_5_q, and_2_out);
  D_Flip_Flop d_ff_1 (.D(j_k_ff_1_q), .clk(hour_plus), .Q(hour_a1));  // open: Qn, preset, reset
  D_Flip_Flop d_ff_2 (.D(j_k_ff_2_q), .clk(hour_plus), .Q(hour_1a));  // open: Qn, preset, reset
  J_K_Flip_Flop #(.trigger("falling")) j_k_ff_3 (
    .J(and_2_out), .K(and_2_out), .clk(hour_plus), .Q(j_k_ff_3_q), .reset(or_2_out));  // open: Qn, preset
  and and_2 (and_2_out, or_1_out, j_k_ff_1_q);
  D_Flip_Flop d_ff_3 (.D(j_k_ff_3_q), .clk(hour_plus), .Q(hour_a2));  // open: Qn, preset, reset
  and and_3 (and_3_out, and_2_out, j_k_ff_3_q);
  J_K_Flip_Flop #(.trigger("falling")) j_k_ff_4 (
    .J(and_3_out), .K(and_3_out), .clk(hour_plus), .Q(j_k_ff_4_q), .reset(or_2_out));  // open: Qn, preset
  D_Flip_Flop d_ff_4 (.D(j_k_ff_4_q), .clk(hour_plus), .Q(hour_a4));  // open: Qn, preset, reset
  and and_4 (and_4_out, hour_1a, j_k_ff_1_q, j_k_ff_3_q);
  and and_5 (and_5_out, and_3_out, j_k_ff_4_q);
  D_Flip_Flop d_ff_5 (.D(j_k_ff_5_q), .clk(hour_plus), .Q(hour_a8));  // open: Qn, preset, reset
  J_K_Flip_Flop #(.trigger("falling")) j_k_ff_5 (
    .J(and_5_out), .K(and_5_out), .clk(hour_plus), .Q(j_k_ff_5_q), .reset(or_2_out));  // open: Qn, preset
  and and_6 (and_6_out, j_k_ff_3_q, j_k_ff_5_q);
  or or_2 (or_2_out, and_6_out, and_4_out);
  Hex_Digit_Display hex_digit_display_1 (.value({{3{in_3}}, hour_1a}));  // open: dp
  and and_7 (and_7_out, hour_1a, or_1_out, j_k_ff_1_q);
  Hex_Digit_Display hex_digit_display_2 (.value({hour_a8, hour_a4, hour_a2, hour_a1}));  // open: dp
  J_K_Flip_Flop j_k_ff_6 (.J(and_7_out), .K(and_7_out), .clk(hour_plus), .Q(j_k_ff_6_q));  // open: Qn, preset, reset
  D_Flip_Flop d_ff_6 (.D(j_k_ff_6_q), .clk(hour_plus), .Q(ampm));  // open: Qn, preset, reset
  LED led_1 (.in(ampm));

  // Notes on the sheet:
  //   Change at 9:59
  //   11h59m
endmodule

module full_clock (
  input  in_1,
  input  in_2,
  input  set_alarm,
  input  hour_plus,
  input  power,
  input  set_time,
  input  minute_plus,
  input  set_ampm,
  output [3:0] mainhour_0a,
  output [3:0] mainhour_a0,
  output [3:0] mainmin_0a,
  output [3:0] mainmin_a0,
  output s_hour_1a,
  output a_hour_1a,
  output s_hour_a1,
  output a_hour_a1,
  output s_hour_a2,
  output a_hour_a2,
  output s_hour_a8,
  output a_hour_a8,
  output s_hour_a4,
  output a_hour_a4,
  output a_min_4a,
  output s_min_4a,
  output s_min_2a,
  output a_min_2a,
  output s_min_1a,
  output a_min_1a,
  output s_min_a8,
  output a_min_a8,
  output s_min_a4,
  output a_min_a4,
  output s_min_a2,
  output s_min_a1,
  output a_min_a2,
  output a_min_a1,
  output alarm_ampm,
  output stan_ampm,
  output main_ampm
);

  wire and_1_out, and_2_out, and_3_out, and_4_out, and_5_out, and_6_out, and_7_out, and_8_out, and_9_out,
       and_10_out, and_11_out, and_12_out, and_13_out, and_14_out, and_15_out, and_16_out, and_17_out,
       and_18_out, and_19_out, and_20_out, and_21_out, and_22_out, and_23_out, and_24_out, and_25_out,
       and_26_out, and_27_out, and_28_out, not_1_out;

  and and_1 (and_1_out, set_alarm, hour_plus);
  and and_2 (and_2_out, set_alarm, minute_plus);
  not not_1 (not_1_out, set_alarm);
  standard_clock standard_clock_1 (
    .hour_plus(hour_plus), .power(power), .set_time(set_time), .minute_plus(minute_plus),
    .hour_a4(s_hour_a4), .hour_a8(s_hour_a8), .hour_a2(s_hour_a2), .hour_a1(s_hour_a1), .hour_1a(s_hour_1a),
    .standard_clock_am_pm(stan_ampm), .minute_a1(s_min_a1), .minute_a2(s_min_a2), .minute_a4(s_min_a4),
    .minute_a8(s_min_a8), .minute_1a(s_min_1a), .minute_2a(s_min_2a), .minute_4a(s_min_4a));  // open: in_1, in_3, in_7
  and and_3 (and_3_out, not_1_out, s_hour_1a);
  or or_1 (mainhour_a0[0], and_3_out, and_4_out);
  and and_4 (and_4_out, set_alarm, a_hour_1a);
  or or_2 (mainhour_0a[0], and_5_out, and_6_out);
  and and_5 (and_5_out, not_1_out, s_hour_a1);
  or or_3 (mainhour_0a[1], and_7_out, and_8_out);
  and and_6 (and_6_out, set_alarm, a_hour_a1);
  and and_7 (and_7_out, not_1_out, s_hour_a2);
  and and_8 (and_8_out, set_alarm, a_hour_a2);
  or or_4 (mainhour_0a[2], and_10_out, and_9_out);
  and and_9 (and_9_out, set_alarm, a_hour_a4);
  and and_10 (and_10_out, not_1_out, s_hour_a4);
  or or_5 (mainhour_0a[3], and_11_out, and_13_out);
  and and_11 (and_11_out, not_1_out, s_hour_a8);
  and and_12 (and_12_out, stan_ampm, not_1_out);
  and and_13 (and_13_out, set_alarm, a_hour_a8);
  or or_6 (main_ampm, and_12_out, and_15_out);
  and and_14 (and_14_out, not_1_out, s_min_1a);
  and and_15 (and_15_out, alarm_ampm, set_alarm);
  or or_7 (mainmin_a0[0], and_14_out, and_16_out);
  and and_16 (and_16_out, set_alarm, a_min_1a);
  or or_8 (mainmin_a0[1], and_17_out, and_18_out);
  and and_17 (and_17_out, not_1_out, s_min_2a);
  and and_18 (and_18_out, set_alarm, a_min_2a);
  and and_19 (and_19_out, not_1_out, s_min_4a);
  or or_9 (mainmin_a0[2], and_19_out, and_20_out);
  and and_20 (and_20_out, set_alarm, a_min_4a);
  alarm_clock alarm_clock_1 (
    .hour_plus(and_1_out), .min_plus(and_2_out), .set_ampm_alarm(set_ampm), .hour_a4(a_hour_a4),
    .hour_a8(a_hour_a8), .hour_a2(a_hour_a2), .hour_a1(a_hour_a1), .hour_1a(a_hour_1a), .minute_a1(a_min_a1),
    .minute_a2(a_min_a2), .minute_a4(a_min_a4), .minute_a8(a_min_a8), .Alarm_ampm(alarm_ampm),
    .minute_1a(a_min_1a), .minute_2a(a_min_2a), .minute_4a(a_min_4a));  // open: in_1, in_4, alarm_clock_ampm
  or or_10 (mainmin_0a[0], and_21_out, and_22_out);
  and and_21 (and_21_out, not_1_out, s_min_a1);
  or or_11 (mainmin_0a[1], and_23_out, and_24_out);
  and and_22 (and_22_out, set_alarm, a_min_a1);
  and and_23 (and_23_out, not_1_out, s_min_a2);
  and and_24 (and_24_out, set_alarm, a_min_a2);
  or or_12 (mainmin_0a[2], and_25_out, and_26_out);
  and and_25 (and_25_out, not_1_out, s_min_a4);
  and and_26 (and_26_out, set_alarm, a_min_a4);
  and and_27 (and_27_out, not_1_out, s_min_a8);
  or or_13 (mainmin_0a[3], and_27_out, and_28_out);
  and and_28 (and_28_out, set_alarm, a_min_a8);

  assign mainhour_a0[3:1] = {3{in_1}};
  assign mainmin_a0[3] = in_2;
endmodule

module compare (
  input  set_alarm,
  input  hour_plus,
  input  power,
  input  set_time,
  input  minute_plus,
  input  set_ampm,
  input  alarm_on,
  output [3:0] main_min_a0,
  output [3:0] main_min_0a,
  output [3:0] main_hour_a0,
  output [3:0] main_hour_0a,
  output main_alarm,
  output main_ampm
);

  wire and_1_out, and_2_out, and_3_out, and_4_out, full_clock_1_a_hour_1a, full_clock_1_a_hour_a1,
       full_clock_1_a_hour_a2, full_clock_1_a_hour_a4, full_clock_1_a_hour_a8, full_clock_1_a_min_1a,
       full_clock_1_a_min_2a, full_clock_1_a_min_4a, full_clock_1_a_min_a1, full_clock_1_a_min_a2,
       full_clock_1_a_min_a4, full_clock_1_a_min_a8, full_clock_1_alarm_ampm, full_clock_1_s_hour_1a,
       full_clock_1_s_hour_a1, full_clock_1_s_hour_a2, full_clock_1_s_hour_a4, full_clock_1_s_hour_a8,
       full_clock_1_s_min_1a, full_clock_1_s_min_2a, full_clock_1_s_min_4a, full_clock_1_s_min_a1,
       full_clock_1_s_min_a2, full_clock_1_s_min_a4, full_clock_1_s_min_a8, full_clock_1_stan_ampm,
       j_k_ff_1_q, not_1_out, not_2_out, not_3_out, not_4_out, not_5_out, not_6_out, not_7_out, not_8_out,
       not_9_out, not_10_out, not_11_out, not_12_out, not_13_out, not_14_out, xor_1_out, xor_2_out,
       xor_3_out, xor_4_out, xor_5_out, xor_6_out, xor_7_out, xor_8_out, xor_9_out, xor_10_out, xor_11_out,
       xor_12_out, xor_13_out;

  full_clock full_clock_1 (
    .set_alarm(set_alarm), .hour_plus(hour_plus), .power(power), .set_time(set_time),
    .minute_plus(minute_plus), .set_ampm(set_ampm), .mainhour_0a(main_hour_0a), .mainhour_a0(main_hour_a0),
    .mainmin_0a(main_min_0a), .mainmin_a0(main_min_a0), .s_hour_1a(full_clock_1_s_hour_1a),
    .a_hour_1a(full_clock_1_a_hour_1a), .s_hour_a1(full_clock_1_s_hour_a1),
    .a_hour_a1(full_clock_1_a_hour_a1), .s_hour_a2(full_clock_1_s_hour_a2),
    .a_hour_a2(full_clock_1_a_hour_a2), .s_hour_a8(full_clock_1_s_hour_a8),
    .a_hour_a8(full_clock_1_a_hour_a8), .s_hour_a4(full_clock_1_s_hour_a4),
    .a_hour_a4(full_clock_1_a_hour_a4), .a_min_4a(full_clock_1_a_min_4a), .s_min_4a(full_clock_1_s_min_4a),
    .s_min_2a(full_clock_1_s_min_2a), .a_min_2a(full_clock_1_a_min_2a), .s_min_1a(full_clock_1_s_min_1a),
    .a_min_1a(full_clock_1_a_min_1a), .s_min_a8(full_clock_1_s_min_a8), .a_min_a8(full_clock_1_a_min_a8),
    .s_min_a4(full_clock_1_s_min_a4), .a_min_a4(full_clock_1_a_min_a4), .s_min_a2(full_clock_1_s_min_a2),
    .s_min_a1(full_clock_1_s_min_a1), .a_min_a2(full_clock_1_a_min_a2), .a_min_a1(full_clock_1_a_min_a1),
    .alarm_ampm(full_clock_1_alarm_ampm), .stan_ampm(full_clock_1_stan_ampm), .main_ampm(main_ampm));  // open: in_1, in_2
  xor xor_1 (xor_1_out, full_clock_1_s_hour_1a, full_clock_1_a_hour_1a);
  xor xor_2 (xor_2_out, full_clock_1_s_hour_a1, full_clock_1_a_hour_a1);
  xor xor_3 (xor_3_out, full_clock_1_s_hour_a2, full_clock_1_a_hour_a2);
  buf xor_4 (xor_4_out, full_clock_1_a_hour_a8);  // XOR_Gate
  xor xor_5 (xor_5_out, full_clock_1_s_hour_a4, full_clock_1_a_hour_a4);
  xor xor_6 (xor_6_out, full_clock_1_a_min_4a, full_clock_1_s_min_4a);
  xor xor_7 (xor_7_out, full_clock_1_s_min_2a, full_clock_1_a_min_2a);
  xor xor_8 (xor_8_out, full_clock_1_s_min_1a, full_clock_1_a_min_1a);
  xor xor_9 (xor_9_out, full_clock_1_s_min_a8, full_clock_1_a_min_a8);
  xor xor_10 (xor_10_out, full_clock_1_s_min_a4, full_clock_1_a_min_a4);
  xor xor_11 (xor_11_out, full_clock_1_s_min_a2, full_clock_1_a_min_a2);
  xor xor_12 (xor_12_out, full_clock_1_s_min_a1, full_clock_1_a_min_a1);
  not not_1 (not_1_out, xor_1_out);
  not not_2 (not_2_out, xor_2_out);
  not not_3 (not_3_out, xor_3_out);
  not not_4 (not_4_out, xor_4_out);
  not not_5 (not_5_out, xor_5_out);
  not not_6 (not_6_out, xor_6_out);
  not not_7 (not_7_out, xor_7_out);
  not not_8 (not_8_out, xor_8_out);
  not not_9 (not_9_out, xor_9_out);
  not not_10 (not_10_out, xor_10_out);
  not not_11 (not_11_out, xor_11_out);
  not not_12 (not_12_out, xor_12_out);
  xor xor_13 (xor_13_out, full_clock_1_alarm_ampm, full_clock_1_stan_ampm);
  and and_1 (and_1_out, not_2_out, not_3_out, not_4_out, not_5_out);
  and and_2 (and_2_out, not_6_out, not_7_out, not_8_out);
  and and_3 (and_3_out, not_9_out, not_10_out, not_11_out, not_12_out);
  not not_13 (not_13_out, xor_13_out);
  and and_4 (and_4_out, not_1_out, and_1_out, and_2_out, and_3_out, not_13_out);
  J_K_Flip_Flop j_k_ff_1 (
    .J(and_4_out), .K(and_4_out), .clk(and_4_out), .Q(j_k_ff_1_q), .reset(not_14_out));  // open: Qn, preset
  not not_14 (not_14_out, alarm_on);
  and and_5 (main_alarm, j_k_ff_1_q, alarm_on);
endmodule

module standard_clock (
  input  in_1,
  input  hour_plus,
  input  in_3,
  input  power,
  input  set_time,
  input  minute_plus,
  input  in_7,
  output hour_a4,
  output hour_a8,
  output hour_a2,
  output hour_a1,
  output hour_1a,
  output standard_clock_am_pm,
  output minute_a1,
  output minute_a2,
  output minute_a4,
  output minute_a8,
  output minute_1a,
  output minute_2a,
  output minute_4a
);

  wire minute_1_reach59, not_1_out;

  minute minute_1 (
    .power(power), .set_time(set_time), .minute_plus(minute_plus), .in_4(in_3), .reach59(minute_1_reach59),
    .minute_a1(minute_a1), .minute_a2(minute_a2), .minute_a4(minute_a4), .minute_a8(minute_a8),
    .minute_1a(minute_1a), .minute_2a(minute_2a), .minute_4a(minute_4a));
  hour hour_1 (
    .input_at_59(minute_1_reach59), .hour_plus(hour_plus), .set_time(set_time), .in_4(in_3),
    .hour_1a(hour_1a), .ampm(standard_clock_am_pm), .hour_a1(hour_a1), .hour_a2(hour_a2), .hour_a4(hour_a4),
    .hour_a8(hour_a8));
  Hex_Digit_Display hex_digit_display_1 (.value({{3{in_1}}, hour_1a}));  // open: dp
  Hex_Digit_Display hex_digit_display_2 (.value({hour_a8, hour_a4, hour_a2, hour_a1}));  // open: dp
  Hex_Digit_Display hex_digit_display_3 (.value({in_7, minute_4a, minute_2a, minute_1a}));  // open: dp
  Hex_Digit_Display hex_digit_display_4 (.value({minute_a8, minute_a4, minute_a2, minute_a1}));  // open: dp
  not not_1 (not_1_out, standard_clock_am_pm);
  LED led_1 (.in(standard_clock_am_pm));
  LED led_2 (.in(not_1_out));

  // Notes on the sheet:
  //   :
  //   AM
  //   PM
endmodule
