// Logisim project lab1.circ as structural Verilog: 1 circuit, main circuit main
module main (
  input  Pin1,
  input  in_2,
  input  Input_1,
  input  Input_2,
  input  Pin_1,
  input  Pin_1_2,
  input  in_7,
  input  Input_C__Ci,
  input  Input_1_2,
  input  Input_2_2
);

  wire and_1_out, and_2_out, and_3_out, and_4_out, nand_1_out, not_1_out, or_1_out, xor_1_out, xor_2_out,
       xor_3_out;

  not not_1 (not_1_out, Pin_1);
  nand nand_1 (nand_1_out, Pin_1_2, in_7);
  xor xor_1 (xor_1_out, Input_1_2, Input_2_2);
  and and_1 (and_1_out, Input_1_2, Input_2_2);
  and and_2 (and_2_out, Pin1, in_2);
  LED led_1 (.in(nand_1_out));
  LED led_2 (.in(and_2_out));
  LED led_3 (.in(not_1_out));
  xor xor_2 (xor_2_out, Input_C__Ci, xor_1_out);
  and and_3 (and_3_out, Input_C__Ci, xor_1_out);
  LED led_4 (.in(xor_2_out));
  or or_1 (or_1_out, and_3_out, and_1_out);
  LED led_5 (.in(or_1_out));
  xor xor_3 (xor_3_out, Input_1, Input_2);
  and and_4 (and_4_out, Input_2, Input_1);
  LED led_6 (.in(xor_3_out));
  LED led_7 (.in(and_4_out));

  // Notes on the sheet:
  //   Pin 2 
  //   Pin 2 
  //   Sum Output 
  //   Carry Output 
  //   Sum Output 
  //   Carry Output 
endmodule
