// Logisim project Week2.circ as structural Verilog: 1 circuit, main circuit main
module main (
  input  in_1,
  input  in_2,
  input  Input_A,
  input  Input_B,
  input  Input_A_2,
  input  Input_B_2,
  input  in_7,
  input  Input_B_3,
  input  Set,
  input  Reset,
  input  J,
  input  K
);

  wire and_1_out, and_2_out, and_3_out, and_4_out, and_5_out, and_6_out, and_7_out, clock_1_out, nand_1_out,
       nand_2_out, nand_3_out, nand_4_out, nor_1_out, nor_2_out, or_1_out, or_2_out, or_3_out, xor_1_out,
       xor_2_out, xor_3_out, xor_4_out, xor_5_out, xor_6_out, xor_7_out;

  Clock clock_1 (.out(clock_1_out));
  and and_1 (and_1_out, in_1, in_2);
  xor xor_1 (xor_1_out, Input_A, Input_B);
  and and_2 (and_2_out, Input_A, Input_B);
  xor xor_2 (xor_2_out, Input_A_2, Input_B_2);
  and and_3 (and_3_out, Input_A_2, Input_B_2);
  xor xor_3 (xor_3_out, in_7, Input_B_3);
  and and_4 (and_4_out, in_7, Input_B_3);
  xor xor_4 (xor_4_out, in_1, in_2);
  nor nor_1 (nor_1_out, Set, nor_2_out);
  nor nor_2 (nor_2_out, nor_1_out, Reset);
  nand nand_1 (nand_1_out, nand_4_out, clock_1_out);
  nand nand_2 (nand_2_out, clock_1_out, nand_3_out);
  xor xor_5 (xor_5_out, and_1_out, xor_1_out);
  and and_5 (and_5_out, and_1_out, xor_1_out);
  xor xor_6 (xor_6_out, or_1_out, xor_2_out);
  and and_6 (and_6_out, or_1_out, xor_2_out);
  xor xor_7 (xor_7_out, or_2_out, xor_3_out);
  and and_7 (and_7_out, or_2_out, xor_3_out);
  LED led_1 (.in(nor_2_out));
  J_K_Flip_Flop j_k_ff_1 ();  // open: J, K, clk, Q, Qn, preset, reset
  LED led_2 (.in(nor_1_out));
  nand nand_3 (nand_3_out, nand_1_out, nand_4_out);
  nand nand_4 (nand_4_out, nand_3_out, nand_2_out);
  LED led_3 (.in(xor_4_out));
  or or_1 (or_1_out, and_5_out, and_2_out);
  or or_2 (or_2_out, and_6_out, and_3_out);
  or or_3 (or_3_out, and_7_out, and_4_out);
  LED led_4 (.in(xor_5_out));
  LED led_5 (.in(xor_6_out));
  LED led_6 (.in(xor_7_out));
  LED led_7 (.in(or_3_out));
  LED led_8 (.in(nand_3_out));
  LED led_9 (.in(nand_4_out));

  // Notes on the sheet:
  //   Input A
  //   Input B
  //   Input A
  //   Q
  //   Q'
  //   Output 0
  //   Output 1
  //   Output 2
  //   Output  3 
  //   Output  C
  //   Q
  //   Q'
endmodule
