// Logisim project lab3.circ as structural Verilog: 1 circuit, main circuit main
module main (
  input  in_1,
  input  in_2,
  input  in_3,
  input  in_4,
  input  Enable,
  input  Reset,
  input  Enable_2,
  input  in_8,
  input  in_9,
  input  in_10,
  input  in_11,
  input  Enable_3,
  input  in_13
);

  wire and_1_out, and_2_out, and_3_out, and_4_out, and_5_out, clock_1_out, clock_2_out, clock_3_out,
       clock_4_out, clock_5_out, d_ff_1_q, d_ff_2_q, d_ff_4_q, d_ff_7_q, j_k_ff_1_q, j_k_ff_2_q, j_k_ff_3_q,
       j_k_ff_4_q, j_k_ff_5_q, j_k_ff_6_q, j_k_ff_7_q, j_k_ff_8_q, j_k_ff_9_q, j_k_ff_10_q, j_k_ff_11_q,
       j_k_ff_12_q;
  wire [2:0] d_ff_3_q, d_ff_8_q;

  Clock clock_1 (.out(clock_1_out));
  Clock clock_2 (.out(clock_2_out));
  and and_1 (and_1_out, j_k_ff_3_q, j_k_ff_6_q);
  J_K_Flip_Flop #(.trigger("falling")) j_k_ff_1 (
    .J(and_1_out), .K(and_1_out), .clk(clock_3_out), .Q(j_k_ff_1_q), .reset(in_8));  // open: Qn, preset
  LED led_1 (.in(j_k_ff_1_q));
  D_Flip_Flop d_ff_1 (.D(in_1), .clk(clock_1_out), .Q(d_ff_1_q), .reset(Reset));  // open: Qn, preset
  J_K_Flip_Flop #(.trigger("falling")) j_k_ff_2 (
    .J(and_2_out), .K(and_2_out), .clk(clock_4_out), .Q(j_k_ff_2_q), .reset(and_3_out));  // open: Qn, preset
  D_Flip_Flop d_ff_2 (.D(in_2), .clk(clock_1_out), .Q(d_ff_2_q), .reset(Reset));  // open: Qn, preset
  LED led_2 (.in(d_ff_1_q));
  J_K_Flip_Flop #(.trigger("falling")) j_k_ff_3 (
    .J(j_k_ff_6_q), .K(j_k_ff_6_q), .clk(clock_3_out), .Q(j_k_ff_3_q), .reset(in_8));  // open: Qn, preset
  LED led_3 (.in(j_k_ff_3_q));
  J_K_Flip_Flop j_k_ff_4 (.J(in_10), .K(in_10), .clk(j_k_ff_7_q), .Q(j_k_ff_4_q), .reset(in_11));  // open: Qn, preset
  and and_2 (and_2_out, j_k_ff_5_q, j_k_ff_8_q);
  LED led_4 (.in(j_k_ff_2_q));
  D_Flip_Flop d_ff_3 (.D(j_k_ff_8_q), .clk(clock_4_out), .Q(d_ff_3_q[0]));  // open: Qn, preset, reset
  LED led_5 (.in(d_ff_2_q));
  LED led_6 (.in(j_k_ff_4_q));
  J_K_Flip_Flop #(.trigger("falling")) j_k_ff_5 (
    .J(j_k_ff_8_q), .K(j_k_ff_8_q), .clk(clock_4_out), .Q(j_k_ff_5_q), .reset(and_3_out));  // open: Qn, preset
  D_Flip_Flop d_ff_4 (.D(in_3), .clk(clock_1_out), .Q(d_ff_4_q), .reset(Reset));  // open: Qn, preset
  J_K_Flip_Flop #(.trigger("falling")) j_k_ff_6 (
    .J(Enable_2), .K(Enable_2), .clk(clock_3_out), .Q(j_k_ff_6_q), .reset(in_8));  // open: Qn, preset
  J_K_Flip_Flop j_k_ff_7 (.J(in_10), .K(in_10), .clk(j_k_ff_9_q), .Q(j_k_ff_7_q), .reset(in_11));  // open: Qn, preset
  LED led_7 (.in(j_k_ff_5_q));
  D_Flip_Flop d_ff_5 (.D(j_k_ff_5_q), .clk(clock_4_out), .Q(d_ff_3_q[1]));  // open: Qn, preset, reset
  LED led_8 (.in(d_ff_4_q));
  LED led_9 (.in(j_k_ff_6_q));
  LED led_10 (.in(j_k_ff_7_q));
  J_K_Flip_Flop #(.trigger("falling")) j_k_ff_8 (
    .J(Enable_3), .K(Enable_3), .clk(clock_4_out), .Q(j_k_ff_8_q), .reset(and_3_out));  // open: Qn, preset
  and and_3 (and_3_out, j_k_ff_2_q, j_k_ff_5_q);
  D_Flip_Flop d_ff_6 (.D(j_k_ff_2_q), .clk(clock_4_out), .Q(d_ff_3_q[2]));  // open: Qn, preset, reset
  D_Flip_Flop d_ff_7 (.D(in_4), .clk(clock_1_out), .Q(d_ff_7_q), .reset(Reset));  // open: Qn, preset
  LED led_11 (.in(d_ff_7_q));
  Clock clock_3 (.out(clock_3_out));
  J_K_Flip_Flop j_k_ff_9 (.J(in_10), .K(in_10), .clk(clock_2_out), .Q(j_k_ff_9_q), .reset(in_11));  // open: Qn, preset
  LED led_12 (.in(j_k_ff_8_q));
  Clock clock_4 (.out(clock_4_out));
  LED led_13 (.in(j_k_ff_9_q));
  Hex_Digit_Display hex_digit_display_1 (.value({in_13, d_ff_3_q}));  // open: dp
  J_K_Flip_Flop #(.trigger("falling")) j_k_ff_10 (
    .J(and_4_out), .K(and_4_out), .clk(clock_5_out), .Q(j_k_ff_10_q), .reset(and_5_out));  // open: Qn, preset
  and and_4 (and_4_out, j_k_ff_11_q, j_k_ff_12_q);
  LED led_14 (.in(j_k_ff_10_q));
  D_Flip_Flop d_ff_8 (.D(j_k_ff_12_q), .clk(clock_5_out), .Q(d_ff_8_q[0]));  // open: Qn, preset, reset
  J_K_Flip_Flop #(.trigger("falling")) j_k_ff_11 (
    .J(j_k_ff_12_q), .K(j_k_ff_12_q), .clk(clock_5_out), .Q(j_k_ff_11_q), .reset(and_5_out));  // open: Qn, preset
  LED led_15 (.in(j_k_ff_11_q));
  D_Flip_Flop d_ff_9 (.D(j_k_ff_11_q), .clk(clock_5_out), .Q(d_ff_8_q[1]));  // open: Qn, preset, reset
  J_K_Flip_Flop #(.trigger("falling")) j_k_ff_12 (
    .J(Enable), .K(Enable), .clk(clock_5_out), .Q(j_k_ff_12_q), .reset(and_5_out));  // open: Qn, preset
  and and_5 (and_5_out, j_k_ff_10_q, j_k_ff_11_q);
  D_Flip_Flop d_ff_10 (.D(j_k_ff_10_q), .clk(clock_5_out), .Q(d_ff_8_q[2]));  // open: Qn, preset, reset
  LED led_16 (.in(j_k_ff_12_q));
  Clock clock_5 (.out(clock_5_out));
  Hex_Digit_Display hex_digit_display_2 (.value({in_9, d_ff_8_q}));  // open: dp

  // Notes on the sheet:
  //   Clock
  //   Data
  //   4
  //   8
  //   2
  //   4
  //   4
  //   4
  //   2
  //   2
  //   1
  //   2
  //   1
  //   Clock
  //   1
  //   1
  //   Clock
  //   Reset
  //   4
  //   2
  //   1
  //   Clock
  //   Reset
endmodule
